// Logisim project contador_simple.circ as structural Verilog: 1 circuit, main circuit main
module main (
  input  reset,
  output out_2,
  output out_3,
  output out_4,
  output out_5
);

  wire and_1_out, and_2_out, clock_1_out, d_ff_1_qn, xor_1_out, xor_2_out, xor_3_out;

  and and_1 (and_1_out, out_2, out_3);
  and and_2 (and_2_out, out_4, and_1_out);
  xor xor_1 (xor_1_out, out_3, out_2);
  xor xor_2 (xor_2_out, out_4, and_1_out);
  xor xor_3 (xor_3_out, out_5, and_2_out);
  Clock clock_1 (.out(clock_1_out));
  D_Flip_Flop d_ff_1 (.D(d_ff_1_qn), .clk(clock_1_out), .Q(out_2), .Qn(d_ff_1_qn), .preset(1'b0), .reset(reset));
  D_Flip_Flop d_ff_2 (.D(xor_1_out), .clk(clock_1_out), .Q(out_3), .preset(1'b0), .reset(reset));  // open: Qn
  D_Flip_Flop d_ff_3 (.D(xor_2_out), .clk(clock_1_out), .Q(out_4), .preset(1'b0), .reset(reset));  // open: Qn
  D_Flip_Flop d_ff_4 (.D(xor_3_out), .clk(clock_1_out), .Q(out_5), .preset(1'b0), .reset(reset));  // open: Qn
endmodule
